// Logisim project SubCircuits.circ as structural Verilog: 15 circuits, main circuit main
module main (
  input  in_1,
  input  in_2,
  input  in_3,
  input  in_4,
  input  [7:0] Input,
  input  in_6,
  input  in_7,
  input  A0,
  input  A1,
  input  X,
  input  A0_2,
  input  A1_2,
  input  A2,
  input  A3,
  input  X0,
  input  X1,
  output [7:0] adderIndi,
  output out_18,
  output [7:0] resIndi,
  output out_20,
  output Out1,
  output [7:0] Sign_and_magnitude,
  output out_23,
  output out_24,
  output out_25
);

  NAND nand_1 (.A(in_1), .B(in_2), .Y(out_18));
  NOR nor_1 (.A(in_3), .B(in_4), .Y(out_20));
  XOR xor_1 (.A(in_6), .B(in_7), .Y(out_23));
  _2_to_1_MUX u_2_to_1_mux_1 (.A0(A0), .A1(A1), .X(X), .Y(out_24));
  _4_to_1_MUX u_4_to_1_mux_1 (.A0(A0_2), .A1(A1_2), .A2(A2), .A3(A3), .X1(X0), .X0(X1), .Y(out_25));
  AddMachine addmachine_1 (.out_1(adderIndi), .out_2(resIndi));
  Ex4 ex4_1 (.In(Input), .Out1(Out1), .Out2(Sign_and_magnitude));
endmodule

// TestNAND
module NAND (
  input  A,
  input  B,
  output Y
);

  wire and_1_out;

  and and_1 (and_1_out, A, B);
  not not_1 (Y, and_1_out);
endmodule

// TestNOR
module NOR (
  input  A,
  input  B,
  output Y
);

  wire or_1_out;

  or or_1 (or_1_out, A, B);
  not not_1 (Y, or_1_out);
endmodule

// TestXOR
module XOR (
  input  A,
  input  B,
  output Y
);

  wire and_1_out, and_2_out, not_1_out, not_2_out;

  not not_1 (not_1_out, A);
  not not_2 (not_2_out, B);
  and and_1 (and_1_out, A, not_2_out);
  and and_2 (and_2_out, not_1_out, B);
  or or_1 (Y, and_1_out, and_2_out);
endmodule

// 2-to-1
module _2_to_1_MUX (
  input  A0,
  input  A1,
  input  X,
  output Y
);

  wire and_1_out, and_2_out, not_1_out;

  not not_1 (not_1_out, X);
  and and_1 (and_1_out, A0, not_1_out);
  and and_2 (and_2_out, X, A1);
  or or_1 (Y, and_1_out, and_2_out);
endmodule

// 4-to-1
module _4_to_1_MUX (
  input  A0,
  input  A1,
  input  A2,
  input  A3,
  input  X1,
  input  X0,
  output Y
);

  wire n2_to_1_mux_1_y, n2_to_1_mux_2_y;

  _2_to_1_MUX u_2_to_1_mux_1 (.A0(A0), .A1(A1), .X(X0), .Y(n2_to_1_mux_1_y));
  _2_to_1_MUX u_2_to_1_mux_2 (.A0(A2), .A1(A3), .X(X0), .Y(n2_to_1_mux_2_y));
  _2_to_1_MUX u_2_to_1_mux_3 (.A0(n2_to_1_mux_1_y), .A1(n2_to_1_mux_2_y), .X(X1), .Y(Y));
endmodule

// AddMachine1
module AddMachine (
  output [7:0] out_1,
  output [7:0] out_2
);

  wire clk_out;

  Adder adder_1 (.a(8'h1), .b(out_2), .out(out_1));  // open: cin, cout
  Clock clk (.out(clk_out));
  Register register_1 (.D(out_1), .en(1'b1), .Q(out_2), .clk(clk_out));  // open: clr
endmodule

// Splitter
module Ex4 (
  input  [7:0] In,
  output Out1,
  output [7:0] Out2
);

  not not_1 (Out2[7], In[7]);
  and and_1 (Out1, In[0], In[7]);

  assign Out2[6:0] = In[6:0];
endmodule

module split_into_16 (
  input  [15:0] in_1,
  output out_2,
  output out_3,
  output out_4,
  output out_5,
  output out_6,
  output out_7,
  output out_8,
  output out_9,
  output out_10,
  output out_11,
  output out_12,
  output out_13,
  output out_14,
  output out_15,
  output out_16,
  output out_17
);


  assign out_2 = in_1[0];
  assign out_3 = in_1[1];
  assign out_4 = in_1[2];
  assign out_5 = in_1[3];
  assign out_6 = in_1[4];
  assign out_7 = in_1[5];
  assign out_8 = in_1[6];
  assign out_9 = in_1[7];
  assign out_10 = in_1[8];
  assign out_11 = in_1[9];
  assign out_12 = in_1[10];
  assign out_13 = in_1[11];
  assign out_14 = in_1[12];
  assign out_15 = in_1[13];
  assign out_16 = in_1[14];
  assign out_17 = in_1[15];
endmodule

// 8
module rotr_8 (
  input  [15:0] in_1,
  output [15:0] out_2
);

  wire [15:0] bit_extender_1_out, bit_extender_2_out, multiplier_1_out;

  assign bit_extender_1_out = {{8{1'b0}}, in_1[7:0]};  // Bit_Extender bit_extender_1
  assign bit_extender_2_out = {{8{1'b0}}, in_1[15:8]};  // Bit_Extender bit_extender_2
  Multiplier #(.width(16)) multiplier_1 (
    .a(16'h100), .b(bit_extender_1_out), .out(multiplier_1_out));  // open: cin, cout
  Adder #(.width(16)) adder_1 (.a(multiplier_1_out), .b(bit_extender_2_out), .out(out_2));  // open: cin, cout
endmodule

// 4
module rotr_4 (
  input  [15:0] in_1,
  output [15:0] out_2
);

  wire [15:0] bit_extender_1_out, bit_extender_2_out, multiplier_1_out;

  assign bit_extender_1_out = {{12{1'b0}}, in_1[3:0]};  // Bit_Extender bit_extender_1
  assign bit_extender_2_out = {{4{1'b0}}, in_1[15:4]};  // Bit_Extender bit_extender_2
  Multiplier #(.width(16)) multiplier_1 (
    .a(16'h1000), .b(bit_extender_1_out), .out(multiplier_1_out));  // open: cin, cout
  Adder #(.width(16)) adder_1 (.a(multiplier_1_out), .b(bit_extender_2_out), .out(out_2));  // open: cin, cout
endmodule

// 2
module rotr_2 (
  input  [15:0] in_1,
  output [15:0] out_2
);

  wire [15:0] bit_extender_1_out, bit_extender_2_out, multiplier_1_out;

  assign bit_extender_1_out = {{14{1'b0}}, in_1[1:0]};  // Bit_Extender bit_extender_1
  assign bit_extender_2_out = {{2{1'b0}}, in_1[15:2]};  // Bit_Extender bit_extender_2
  Multiplier #(.width(16)) multiplier_1 (
    .a(16'h4000), .b(bit_extender_1_out), .out(multiplier_1_out));  // open: cin, cout
  Adder #(.width(16)) adder_1 (.a(multiplier_1_out), .b(bit_extender_2_out), .out(out_2));  // open: cin, cout
endmodule

// 1
module rotr_1 (
  input  [15:0] in_1,
  output [15:0] out_2
);

  wire [15:0] bit_extender_1_out, bit_extender_2_out, multiplier_1_out;

  assign bit_extender_1_out = {{15{1'b0}}, in_1[0]};  // Bit_Extender bit_extender_1
  assign bit_extender_2_out = {{1{1'b0}}, in_1[15:1]};  // Bit_Extender bit_extender_2
  Multiplier #(.width(16)) multiplier_1 (
    .a(16'h8000), .b(bit_extender_1_out), .out(multiplier_1_out));  // open: cin, cout
  Adder #(.width(16)) adder_1 (.a(multiplier_1_out), .b(bit_extender_2_out), .out(out_2));  // open: cin, cout
endmodule

module rotr (
  input  [15:0] Input_number,
  input  [3:0] Bits_to_shift,
  output [15:0] Output
);

  wire [15:0] rotr_1_1_out_2, rotr_1_2_out_2, rotr_1_3_out_2, rotr_1_4_out_2, rotr_1_5_out_2, rotr_1_6_out_2,
       rotr_1_7_out_2, rotr_1_8_out_2, rotr_2_1_out_2, rotr_2_2_out_2, rotr_2_3_out_2, rotr_2_4_out_2,
       rotr_2_5_out_2, rotr_2_6_out_2, rotr_2_7_out_2, rotr_2_8_out_2, rotr_4_1_out_2, rotr_4_2_out_2,
       rotr_4_3_out_2, rotr_4_4_out_2, rotr_4_5_out_2, rotr_4_6_out_2, rotr_4_7_out_2, rotr_4_8_out_2,
       rotr_8_1_out_2, rotr_8_2_out_2, rotr_8_3_out_2, rotr_8_4_out_2, rotr_8_5_out_2, rotr_8_6_out_2,
       rotr_8_7_out_2, rotr_8_8_out_2;

  rotr_1 rotr_1_1 (.in_1(Input_number), .out_2(rotr_1_1_out_2));
  rotr_2 rotr_2_1 (.in_1(Input_number), .out_2(rotr_2_1_out_2));
  rotr_1 rotr_1_2 (.in_1(rotr_2_2_out_2), .out_2(rotr_1_2_out_2));
  rotr_2 rotr_2_2 (.in_1(Input_number), .out_2(rotr_2_2_out_2));
  rotr_4 rotr_4_1 (.in_1(Input_number), .out_2(rotr_4_1_out_2));
  rotr_1 rotr_1_3 (.in_1(rotr_4_2_out_2), .out_2(rotr_1_3_out_2));
  rotr_4 rotr_4_2 (.in_1(Input_number), .out_2(rotr_4_2_out_2));
  rotr_2 rotr_2_3 (.in_1(rotr_4_3_out_2), .out_2(rotr_2_3_out_2));
  rotr_4 rotr_4_3 (.in_1(Input_number), .out_2(rotr_4_3_out_2));
  rotr_2 rotr_2_4 (.in_1(rotr_4_4_out_2), .out_2(rotr_2_4_out_2));
  rotr_4 rotr_4_4 (.in_1(Input_number), .out_2(rotr_4_4_out_2));
  rotr_8 rotr_8_1 (.in_1(Input_number), .out_2(rotr_8_1_out_2));
  rotr_8 rotr_8_2 (.in_1(Input_number), .out_2(rotr_8_2_out_2));
  rotr_1 rotr_1_4 (.in_1(rotr_8_2_out_2), .out_2(rotr_1_4_out_2));
  rotr_8 rotr_8_3 (.in_1(Input_number), .out_2(rotr_8_3_out_2));
  rotr_2 rotr_2_5 (.in_1(rotr_8_3_out_2), .out_2(rotr_2_5_out_2));
  rotr_8 rotr_8_4 (.in_1(Input_number), .out_2(rotr_8_4_out_2));
  rotr_2 rotr_2_6 (.in_1(rotr_8_4_out_2), .out_2(rotr_2_6_out_2));
  rotr_8 rotr_8_5 (.in_1(Input_number), .out_2(rotr_8_5_out_2));
  rotr_4 rotr_4_5 (.in_1(rotr_8_5_out_2), .out_2(rotr_4_5_out_2));
  rotr_8 rotr_8_6 (.in_1(Input_number), .out_2(rotr_8_6_out_2));
  rotr_4 rotr_4_6 (.in_1(rotr_8_6_out_2), .out_2(rotr_4_6_out_2));
  rotr_8 rotr_8_7 (.in_1(Input_number), .out_2(rotr_8_7_out_2));
  rotr_4 rotr_4_7 (.in_1(rotr_8_7_out_2), .out_2(rotr_4_7_out_2));
  rotr_8 rotr_8_8 (.in_1(Input_number), .out_2(rotr_8_8_out_2));
  rotr_4 rotr_4_8 (.in_1(rotr_8_8_out_2), .out_2(rotr_4_8_out_2));
  rotr_1 rotr_1_5 (.in_1(rotr_2_4_out_2), .out_2(rotr_1_5_out_2));
  rotr_1 rotr_1_6 (.in_1(rotr_2_6_out_2), .out_2(rotr_1_6_out_2));
  rotr_1 rotr_1_7 (.in_1(rotr_4_6_out_2), .out_2(rotr_1_7_out_2));
  rotr_2 rotr_2_7 (.in_1(rotr_4_7_out_2), .out_2(rotr_2_7_out_2));
  rotr_1 rotr_1_8 (.in_1(rotr_2_8_out_2), .out_2(rotr_1_8_out_2));
  rotr_2 rotr_2_8 (.in_1(rotr_4_8_out_2), .out_2(rotr_2_8_out_2));
  Multiplexer #(.select(4), .width(16), .enable("false")) multiplexer_1 (
    .in0(Input_number), .in1(rotr_1_1_out_2), .in2(rotr_2_1_out_2), .in3(rotr_1_2_out_2),
    .in4(rotr_4_1_out_2), .in5(rotr_1_3_out_2), .in6(rotr_2_3_out_2), .in7(rotr_1_5_out_2),
    .in8(rotr_8_1_out_2), .in9(rotr_1_4_out_2), .in10(rotr_2_5_out_2), .in11(rotr_1_6_out_2),
    .in12(rotr_4_5_out_2), .in13(rotr_1_7_out_2), .in14(rotr_2_7_out_2), .in15(rotr_1_8_out_2), .out(Output),
    .sel(Bits_to_shift));
endmodule

module rort_simplified (
  input  [15:0] Input_number,
  input  [3:0] Digits_to_shift,
  output [15:0] Output
);

  wire [15:0] multiplexer_1_out, multiplexer_2_out, multiplexer_3_out, rotr_1_1_out_2, rotr_2_1_out_2,
       rotr_4_1_out_2, rotr_8_1_out_2;

  rotr_1 rotr_1_1 (.in_1(Input_number), .out_2(rotr_1_1_out_2));
  Multiplexer #(.width(16), .enable("false")) multiplexer_1 (
    .in0(Input_number), .in1(rotr_1_1_out_2), .out(multiplexer_1_out), .sel(Digits_to_shift[0]));
  rotr_2 rotr_2_1 (.in_1(multiplexer_1_out), .out_2(rotr_2_1_out_2));
  Multiplexer #(.width(16), .enable("false")) multiplexer_2 (
    .in0(multiplexer_1_out), .in1(rotr_2_1_out_2), .out(multiplexer_2_out), .sel(Digits_to_shift[1]));
  rotr_4 rotr_4_1 (.in_1(multiplexer_2_out), .out_2(rotr_4_1_out_2));
  Multiplexer #(.width(16), .enable("false")) multiplexer_3 (
    .in0(multiplexer_2_out), .in1(rotr_4_1_out_2), .out(multiplexer_3_out), .sel(Digits_to_shift[2]));
  rotr_8 rotr_8_1 (.in_1(multiplexer_3_out), .out_2(rotr_8_1_out_2));
  Multiplexer #(.width(16), .enable("false")) multiplexer_4 (
    .in0(multiplexer_3_out), .in1(rotr_8_1_out_2), .out(Output), .sel(Digits_to_shift[3]));
endmodule
