// Logisim project regfile-allregs.circ as structural Verilog: 1 circuit, main circuit main
module main (
  output [7:0] Test,
  output [31:0] ra,
  output [31:0] sp,
  output [31:0] t0,
  output [31:0] t1,
  output [31:0] t2,
  output [31:0] s0,
  output [31:0] s1,
  output [31:0] a0,
  output [31:0] Read_Data_1,
  output [31:0] Read_Data_2
);

  wire clk, RegWEn;
  wire [4:0] rd;
  wire [7:0] adder_1_out;
  wire [9:0] RF_In;
  wire [31:0] Write_Data;

  Register register_1 (.D(adder_1_out), .clk(clk), .Q(Test));  // open: en, clr
  Clock clock_1 (.out(clk));
  Adder adder_1 (.a(8'h1), .b(Test), .out(adder_1_out));  // open: cin, cout
  ROM #(.dataWidth(16)) rs1_rs2_rd_RegWEn (.addr(Test), .data({RegWEn, rd, RF_In}));
  ROM #(.dataWidth(32)) u_Write_Data (.addr(Test), .data(Write_Data));
  regfile_main main_1 (
    .Read_Register_1_rs1(RF_In[4:0]), .Read_Register_2_rs2(RF_In[9:5]), .Write_Register_rd(rd),
    .Write_Data(Write_Data), .Write_Enable(RegWEn), .Clock(clk), .Read_Data_1(Read_Data_1),
    .Read_Data_2(Read_Data_2), .ra(ra), .sp(sp), .t0(t0), .t1(t1), .t2(t2), .s0(s0), .s1(s1), .a0(a0));

  // Other names for the same wires on the sheet: rs1[4:0] = RF_In[4:0]; rs2[4:0] = RF_In[9:5];
  //   RF_In[15:10] = {RegWEn, rd}

  // Notes on the sheet:
  //   contents of rs1_rs2_rd_RegWEn (hex, n*v repeats v):
  //   441 8821 1442 88a2 18a5 94c5 18e6 9cc6 1d07 a0e7 2508 a128 2929 a549 2929 a549 280a 814a
  //   contents of Write_Data (hex, n*v repeats v):
  //   ffffbeef dad fffff00d 5678 afdfadf adfadf adfadf ffffffff a786adc2 98a09723 df89a0ae 28888292 0
  //   53717cfc 9381230 aaa67acb 777d7d89 9f72cd72
  //   Your RegFile must fit here!
  //   There should be no red or blue wires, and the result should not be all X's
endmodule
