// Logisim project alu.circ as structural Verilog: 3 circuits, main circuit alu
module alu (
  input  [31:0] A,
  input  [31:0] B,
  input  [3:0] ALUSel,
  output [31:0] Result
);

  wire comparator_1_lt;
  wire [31:0] add, and32, div32, mulh32, mult32, or32, rem32, sll32, slt32, sra32, srl32, sub32, xor32;

  Adder #(.width(32)) adder_1 (.a(A), .b(B), .out(add));  // open: cin, cout
  assign and32 = A & B;  // AND_Gate and_1, 32 bits wide
  assign or32 = A | B;  // OR_Gate or_1, 32 bits wide
  assign xor32 = A ^ B;  // XOR_Gate xor_1, 32 bits wide
  Comparator #(.width(32)) comparator_1 (.a(A), .b(B), .lt(comparator_1_lt));  // open: gt, eq
  Divider #(.width(32)) divider_1 (.a(A), .b(B), .out(div32));  // open: upper, rem
  Divider #(.width(32)) divider_2 (.a(A), .b(B), .rem(rem32));  // open: out, upper
  Multiplier #(.width(32)) multiplier_1 (.a(A), .b(B), .out(mult32));  // open: cin, cout
  Multiplier #(.width(32)) multiplier_2 (.a(A), .b(B), .cout(mulh32));  // open: out, cin
  Subtractor #(.width(32)) subtractor_1 (.a(A), .b(B), .out(sub32));  // open: bin, bout
  Shifter #(.width(32), .shift("lr")) shifter_1 (.in(A), .\dist (B[4:0]), .out(srl32));
  Shifter #(.width(32), .shift("ar")) shifter_2 (.in(A), .\dist (B[4:0]), .out(sra32));
  Shifter #(.width(32)) shifter_3 (.in(A), .\dist (B[4:0]), .out(sll32));
  assign slt32 = {{31{1'b0}}, comparator_1_lt};  // Bit_Extender bit_extender_1
  Multiplexer #(.select(4), .width(32), .enable("false")) multiplexer_1 (
    .in0(add), .in1(and32), .in2(or32), .in3(xor32), .in4(srl32), .in5(sra32), .in6(sll32), .in7(slt32),
    .in8(div32), .in9(rem32), .in10(mult32), .in11(mulh32), .in12(sub32), .in13(B), .out(Result), .sel(ALUSel));  // open: in14, in15

  // Notes on the sheet:
  //   INPUTS to your circuit
  //   DON'T CHANGE THE LOCATIONS OF THE INPUTS AND OUTPUTS!
  //   OUTPUT from your circuit
endmodule

module uselessadd32 (
  input  [31:0] in_1
);
endmodule

module uselesssra32 (
  input  [31:0] Number,
  input  [31:0] HowFarToShift
);

  wire [31:0] bit_extender_1_out;

  assign bit_extender_1_out = {{31{Number[0]}}, Number[0]};  // Bit_Extender bit_extender_1
  Shifter #(.width(32), .shift("lr")) shifter_1 (.in(Number), .\dist (HowFarToShift[4:0]));  // open: out
  Shifter #(.width(32)) shifter_2 (.in(bit_extender_1_out), .\dist ({5{1'b1}}));  // open: out
endmodule
