// Logisim project cpu.circ as structural Verilog: 4 circuits, main circuit main
module main (
  input  [31:0] INSTRUCTION,
  input  CLOCK,
  output [31:0] FETCH_ADDRESS,
  output [31:0] ra,
  output [31:0] sp,
  output [31:0] t0,
  output [31:0] t1,
  output [31:0] t2,
  output [31:0] s0,
  output [31:0] s1,
  output [31:0] a0
);

  wire ASel_CL, BrEq_BC, BrLT_BC, BrUn_CL, BSel_CL, MemRW_CL, PCSel_CL, RegWEn_CL;
  wire [1:0] WBSel_CL;
  wire [2:0] ImmSel_CL;
  wire [3:0] ALUSel_CL;
  wire [31:0] A_output, ALU_output, B_output, bit_extender_1_out, bit_extender_2_out, DataA, DataB, DataR,
       DataR_MEM, Imm_generator_output, PC_add_4, PC_add_4Bytes, PC_select_output, wb_output;

  Register #(.width(32)) PC (.D(PC_select_output), .en(1'b1), .clk(CLOCK), .Q(FETCH_ADDRESS));  // open: clr
  Multiplexer #(.width(32), .enable("false")) multiplexer_1 (
    .in0(PC_add_4Bytes), .in1(ALU_output), .out(PC_select_output), .sel(PCSel_CL));
  Adder #(.width(32)) adder_1 (.a(FETCH_ADDRESS), .b(32'h1), .out(PC_add_4Bytes));  // open: cin, cout
  controlLogic_ROM controllogic_rom_1 (
    .Instruction(INSTRUCTION), .BrEq(BrEq_BC), .BrLT(BrLT_BC), .WBSel(WBSel_CL), .RegWEn(RegWEn_CL),
    .MemRW(MemRW_CL), .ALUSel(ALUSel_CL), .BSel(BSel_CL), .ASel(ASel_CL), .BrUn(BrUn_CL), .ImmSel(ImmSel_CL),
    .PCSel(PCSel_CL));
  regfile_main main_1 (
    .Read_Register_1_rs1(INSTRUCTION[19:15]), .Read_Register_2_rs2(INSTRUCTION[24:20]),
    .Write_Register_rd(INSTRUCTION[11:7]), .Write_Data(wb_output), .Write_Enable(RegWEn_CL), .Clock(CLOCK),
    .Read_Data_1(DataA), .Read_Data_2(DataB), .ra(ra), .sp(sp), .t0(t0), .t1(t1), .t2(t2), .s0(s0), .s1(s1),
    .a0(a0));
  ImmGenerator immgenerator_1 (
    .Input_Inst31_7(INSTRUCTION[31:7]), .Input_ImmSel_CL(ImmSel_CL), .Output_Imm31_0(Imm_generator_output));
  Multiplexer #(.width(32), .enable("false")) multiplexer_2 (
    .in0(DataA), .in1(FETCH_ADDRESS), .out(A_output), .sel(ASel_CL));
  Multiplexer #(.width(32), .enable("false")) multiplexer_3 (
    .in0(DataB), .in1(Imm_generator_output), .out(B_output), .sel(BSel_CL));
  BranchComparator branchcomparator_1 (
    .Data1(DataA), .Data2(DataB), .BrUnsigned(BrUn_CL), .BrEqual(BrEq_BC), .BrLessThan(BrLT_BC));
  // mem_main MEM: pin names not known; wires that end beside it: ALU_output, DataB, MemRW_CL, CLOCK, DataR_MEM
  alu alu_1 (.A(A_output), .B(B_output), .ALUSel(ALUSel_CL), .Result(ALU_output));
  Multiplexer #(.select(2), .width(32), .enable("false")) multiplexer_4 (
    .in0(DataR), .in1(ALU_output), .in2(PC_add_4), .out(wb_output), .sel(WBSel_CL));  // open: in3
  assign bit_extender_1_out = {{24{DataR_MEM[7]}}, DataR_MEM[7:0]};  // Bit_Extender bit_extender_1
  assign bit_extender_2_out = {{16{DataR_MEM[15]}}, DataR_MEM[15:0]};  // Bit_Extender bit_extender_2
  Multiplexer #(.select(2), .width(32), .enable("false")) multiplexer_5 (
    .in0(bit_extender_1_out), .in1(bit_extender_2_out), .in2(DataR_MEM), .out(DataR), .sel(INSTRUCTION[13:12]));  // open: in3

  // Other names for the same wires on the sheet: a0_reg[31:0] = a0; clk = CLOCK; fetch_addr[31:0] = FETCH_ADDRESS;
  //   AddrD[4:0] = INSTRUCTION[11:7]; Imm_generator_input[24:0] = INSTRUCTION[31:7]; funct3[2:0] = INSTRUCTION[14:12];
  //   Length_choice_bit[1:0] = INSTRUCTION[13:12]; AddrA[4:0] = INSTRUCTION[19:15]; AddrB[4:0] = INSTRUCTION[24:20];
  //   ra_reg[31:0] = ra; s0_reg[31:0] = s0; s1_reg[31:0] = s1; sp_reg[31:0] = sp; t0_reg[31:0] = t0;
  //   t1_reg[31:0] = t1; t2_reg[31:0] = t2

  // Notes on the sheet:
  //   Instruction_Splitter
  //   Output
  //   PCSelect
  //   Inputs/Outputs from run.circ. DO NOT MOVE THESE.
  //   Inputs
  //   MUX_A
  //   MUX_B
  //   Inputs/Outputs from run.circ. DO NOT MOVE THESE.
  //   Length Mux
endmodule

module ImmGenerator (
  input  [24:0] Input_Inst31_7,
  input  [2:0] Input_ImmSel_CL,
  output [31:0] Output_Imm31_0
);

  wire [31:0] I_imm, S_imm, SB_imm, UJ_imm;

  assign S_imm = {{20{Input_Inst31_7[24]}}, {Input_Inst31_7[24:18], Input_Inst31_7[4:0]}};  // Bit_Extender bit_extender_1
  assign SB_imm = {{19{Input_Inst31_7[24]}}, {Input_Inst31_7[24], Input_Inst31_7[0], Input_Inst31_7[23:18], Input_Inst31_7[4:1], 1'b0}};  // Bit_Extender bit_extender_2
  assign I_imm = {{20{Input_Inst31_7[24]}}, Input_Inst31_7[24:13]};  // Bit_Extender bit_extender_3
  assign UJ_imm = {{11{Input_Inst31_7[24]}}, {Input_Inst31_7[24], Input_Inst31_7[12:5], Input_Inst31_7[13], Input_Inst31_7[23:14], 1'b0}};  // Bit_Extender bit_extender_4
  Multiplexer #(.select(3), .width(32), .enable("false")) multiplexer_1 (
    .in0(I_imm), .in1(S_imm), .in2(SB_imm), .in3({Input_Inst31_7[24:5], {12{1'b0}}}), .in4(UJ_imm),
    .out(Output_Imm31_0), .sel(Input_ImmSel_CL));  // open: in5, in6, in7

  // Other names for the same wires on the sheet: imm31_7[24:0] = Input_Inst31_7; U_imm[31:12] = Input_Inst31_7[24:5];
  //   imm31_0[31:0] = Output_Imm31_0; imm_sel[2:0] = Input_ImmSel_CL
endmodule

module controlLogic_ROM (
  input  [31:0] Instruction,
  input  BrEq,
  input  BrLT,
  output [1:0] WBSel,
  output RegWEn,
  output MemRW,
  output [3:0] ALUSel,
  output BSel,
  output ASel,
  output BrUn,
  output [2:0] ImmSel,
  output PCSel
);

  ROM #(.addrWidth(12), .dataWidth(15)) rom_1 (
    .addr({Instruction[2], Instruction[3], Instruction[4], Instruction[5], Instruction[6], Instruction[12], Instruction[13], Instruction[14], Instruction[25], Instruction[30], BrEq, BrLT}),
    .data({PCSel, ImmSel, BrUn, ASel, BSel, ALUSel, MemRW, RegWEn, WBSel}));

  // Other names for the same wires on the sheet: ControlWord[14:0] = {PCSel, ImmSel, BrUn, ASel, BSel, ALUSel, MemRW, RegWEn, WBSel};
  //   Decoder_Output[11:0] = {Instruction[2], Instruction[3], Instruction[4], Instruction[5], Instruction[6], Instruction[12], Instruction[13], Instruction[14], Instruction[25], Instruction[30], BrEq, BrLT};
  //   Instruction31_0[31:0] = Instruction

  // Notes on the sheet:
  //   Instruction Decoder
  //   contents of rom_1 (hex, n*v repeats v):
  //   16*104 16*0 16*104 4*1 12*0 16*104 208*0 16*908 80*0 1300 1300 5300 5300 1300 1300 5300 5300 1300
  //   1300 5300 5300 1300 1300 5300 5300 1300 5300 1300 5300 1300 5300 1300 5300 1300 5300 1300 5300 1300
  //   5300 1300 5300 16*0 1700 5700 1700 5700 1700 5700 1700 5700 1700 5700 1700 5700 1700 5700 1700 5700
  //   5300 5300 1300 1300 5300 5300 1300 1300 5300 5300 1300 1300 5300 5300 1300 1300 48*0 16*105 16*135
  //   16*175 16*125 4*165 12*0 4*145 4*155 24*0 16*115 128*0 4*5 4*c5 4*55 4*0 4*35 4*0 4*85 4*0 4*75 12*0
  //   4*25 4*0 4*95 4*0 4*65 4*0 4*b5 4*0 4*45 28*0 4*15 2316*0 4106 4106 4106 416 12*4106 240*0 128*6306
  //   128*1bd5
endmodule

module BranchComparator (
  input  [31:0] Data1,
  input  [31:0] Data2,
  input  BrUnsigned,
  output BrEqual,
  output BrLessThan
);

  wire comparator_1_lt, comparator_2_lt;

  Comparator #(.width(32)) comparator_1 (.a(Data1), .b(Data2), .lt(comparator_1_lt));  // open: gt, eq
  Comparator #(.width(32), .mode("unsigned")) comparator_2 (
    .a(Data1), .b(Data2), .eq(BrEqual), .lt(comparator_2_lt));  // open: gt
  Multiplexer #(.enable("false")) multiplexer_1 (
    .in0(comparator_1_lt), .in1(comparator_2_lt), .out(BrLessThan), .sel(BrUnsigned));

  // Other names for the same wires on the sheet: BrEq = BrEqual; BrLT = BrLessThan; BrUn = BrUnsigned

  // Notes on the sheet:
  //   Signed
  //   Unsigned
endmodule
