// Logisim project regfile.circ as structural Verilog: 1 circuit, main circuit main
// x9
module main (
  input  [4:0] Read_Register_1_rs1,
  input  [4:0] Read_Register_2_rs2,
  input  [4:0] Write_Register_rd,
  input  [31:0] Write_Data,
  input  Write_Enable,
  input  Clock,
  output [31:0] ra,
  output [31:0] sp,
  output [31:0] t0,
  output [31:0] t1,
  output [31:0] t2,
  output [31:0] s0,
  output [31:0] s1,
  output [31:0] a0,
  output [31:0] Read_Data_1,
  output [31:0] Read_Data_2
);

  wire write_en1, write_en2, write_en5, write_en6, write_en7, write_en8, write_en9, write_en10;
  wire [31:0] write_data1, write_data2, write_data5, write_data6, write_data7, write_data8, write_data9,
       write_data10, x0_data;

  Demultiplexer #(.select(5), .width(32), .enable("false")) demultiplexer_1 (
    .out1(write_data1), .out2(write_data2), .out5(write_data5), .out6(write_data6), .out7(write_data7),
    .out8(write_data8), .out9(write_data9), .out10(write_data10), .in(Write_Data), .sel(Write_Register_rd));  // open: out0, out3, out4, out11, out12, out13, out14, out15, out16, out17, out18, out19, out20, out21, out22, out23, out24, out25, out26, out27, out28, out29, out30, out31
  Demultiplexer #(.select(5), .enable("false")) demultiplexer_2 (
    .out1(write_en1), .out2(write_en2), .out5(write_en5), .out6(write_en6), .out7(write_en7),
    .out8(write_en8), .out9(write_en9), .out10(write_en10), .in(Write_Enable), .sel(Write_Register_rd));  // open: out0, out3, out4, out11, out12, out13, out14, out15, out16, out17, out18, out19, out20, out21, out22, out23, out24, out25, out26, out27, out28, out29, out30, out31
  Register #(.width(32)) x0 (.D({32{1'b0}}), .en(1'b0), .clk(Clock), .Q(x0_data));  // open: clr
  Register #(.width(32)) x1 (.D(write_data1), .en(write_en1), .clk(Clock), .Q(ra));  // open: clr
  Register #(.width(32)) x2 (.D(write_data2), .en(write_en2), .clk(Clock), .Q(sp));  // open: clr
  Register #(.width(32)) x5 (.D(write_data5), .en(write_en5), .clk(Clock), .Q(t0));  // open: clr
  Register #(.width(32)) x6 (.D(write_data6), .en(write_en6), .clk(Clock), .Q(t1));  // open: clr
  Register #(.width(32)) x7 (.D(write_data7), .en(write_en7), .clk(Clock), .Q(t2));  // open: clr
  Register #(.width(32)) x8 (.D(write_data8), .en(write_en8), .clk(Clock), .Q(s0));  // open: clr
  Register #(.width(32)) x9 (.D(write_data9), .en(write_en9), .clk(Clock), .Q(s1));  // open: clr
  Register #(.width(32)) x10 (.D(write_data10), .en(write_en10), .clk(Clock), .Q(a0));  // open: clr
  Multiplexer #(.select(5), .width(32), .enable("false")) multiplexer_1 (
    .in0(x0_data), .in1(ra), .in2(sp), .in5(t0), .in6(t1), .in7(t2), .in8(s0), .in9(s1), .in10(a0),
    .out(Read_Data_1), .sel(Read_Register_1_rs1));  // open: in3, in4, in11, in12, in13, in14, in15, in16, in17, in18, in19, in20, in21, in22, in23, in24, in25, in26, in27, in28, in29, in30, in31
  Multiplexer #(.select(5), .width(32), .enable("false")) multiplexer_2 (
    .in0(x0_data), .in1(ra), .in2(sp), .in5(t0), .in6(t1), .in7(t2), .in8(s0), .in9(s1), .in10(a0),
    .out(Read_Data_2), .sel(Read_Register_2_rs2));  // open: in3, in4, in11, in12, in13, in14, in15, in16, in17, in18, in19, in20, in21, in22, in23, in24, in25, in26, in27, in28, in29, in30, in31

  // Other names for the same wires on the sheet: clk = Clock; read_data1[31:0] = Read_Data_1;
  //   read_data2[31:0] = Read_Data_2; read_reg1[4:0] = Read_Register_1_rs1; read_reg2[4:0] = Read_Register_2_rs2;
  //   write_en = Write_Enable; write_reg[4:0] = Write_Register_rd; x1_data[31:0] = ra; x2_data[31:0] = sp;
  //   x5_data[31:0] = t0; x6_data[31:0] = t1; x7_data[31:0] = t2; x8_data[31:0] = s0; x9_data[31:0] = s1;
  //   x10_data[31:0] = a0

  // Notes on the sheet:
  //   INPUTS to your circuit
  //   DON'T CHANGE THE LOCATIONS OF THE INPUTS AND OUTPUTS!
  //   These are DEBUG/TEST outputs from your circuit.
  //   OUTPUTS from your circuit
endmodule
